// Logisim project goofyahhpc.circ as structural Verilog: 2 circuits, main circuit main
module main (
);

  wire alu_1_jump, button_1_out, clock_1_out, not_1_out, not_2_out;
  wire [4:0] alu_1_location;
  wire [15:0] a_q, alu_1_output, b_q, pc_q, pc_star_q, ram_1_data, ram_star_q, rom_1_data;

  Button button_1 (.out(button_1_out));
  Clock clock_1 (.out(clock_1_out));
  Button reset ();  // open: out
  Register #(.width(16)) ram_star (
    .D(alu_1_output), .en(alu_1_location[0]), .Q(ram_star_q), .clk(clock_1_out));  // open: clr
  RAM #(.addrWidth(16), .dataWidth(16)) ram_1 (
    .addr(ram_star_q), .data(ram_1_data), .sel(1'b1), .clk(clock_1_out), .ld(not_1_out));  // open: clr
  not not_1 (not_1_out, alu_1_location[2]);
  Register #(.width(16)) a (.D(alu_1_output), .en(alu_1_location[4]), .Q(a_q), .clk(clock_1_out));  // open: clr
  alu alu_1 (
    .Memory(ram_1_data), .A(a_q), .B(b_q), .Cmd(rom_1_data), .jump(alu_1_jump), .\output (alu_1_output),
    .location(alu_1_location));
  assign ram_1_data = alu_1_location[2] ? alu_1_output : 16'bz;  // Controlled_Buffer controlled_buffer_1
  Register #(.width(16)) b (.D(alu_1_output), .en(alu_1_location[3]), .Q(b_q), .clk(clock_1_out));  // open: clr
  not not_2 (not_2_out, alu_1_jump);
  Register #(.width(16)) pc_star (
    .D(alu_1_output), .en(alu_1_location[1]), .Q(pc_star_q), .clk(clock_1_out));  // open: clr
  Counter #(.width(16), .max('hffff)) pc (
    .load(alu_1_jump), .D(pc_star_q), .count(not_2_out), .Q(pc_q), .clk(clock_1_out));  // open: carry, clr
  ROM #(.addrWidth(16), .dataWidth(16)) rom_1 (.addr(pc_q), .data(rom_1_data), .sel(1'b1));

  // Notes on the sheet:
  //   contents of rom_1 (hex, n*v repeats v):
  //   15 b820 1 b808 b820 8808 b820 64 b810 b408 b080 8c21 2 b808 b040 3 b808 bc20 1 b808 b040 2 b808 bc20
  //   3 b808 b040 1 b808 b080 8020 7 b810 8007
  //   (동시에 ram*과 ram에 보내면 동기화 안됨)
  //   (ram 가져오는 명령어 사용시 도착지 ram 불가)
endmodule

module alu (
  input  [15:0] A,
  input  [15:0] B,
  input  [15:0] Memory,
  input  [15:0] Cmd,
  output [15:0] \output ,
  output [4:0] location,
  output jump
);

  wire and_1_out, and_4_out, and_5_out, nor_1_out, nor_2_out, not_3_out, or_1_out;
  wire [15:0] adder_1_out, adder_2_out, adder_3_out, adder_4_out, adder_5_out, and_3_out, divider_1_out,
       multiplexer_1_out, multiplexer_2_out, multiplexer_3_out, multiplexer_4_out, multiplexer_5_out,
       multiplexer_6_out, multiplexer_7_out, multiplexer_9_out, multiplier_1_out, not_1_out, not_2_out,
       or_2_out, shifter_1_out, shifter_2_out, xor_1_out;

  Multiplexer #(.select(2), .width(16), .enable("false")) multiplexer_1 (
    .in0(Memory), .in1({16{1'b0}}), .in2(multiplexer_6_out), .in3(multiplexer_9_out),
    .out(multiplexer_1_out), .sel(Cmd[11:10]));
  Adder #(.width(16)) adder_1 (.a(multiplexer_6_out), .b(multiplexer_9_out), .out(adder_1_out));  // open: cin, cout
  nor nor_1 (nor_1_out, multiplexer_7_out[15], multiplexer_7_out[14], multiplexer_7_out[13], multiplexer_7_out[12], multiplexer_7_out[11], multiplexer_7_out[10], multiplexer_7_out[9], multiplexer_7_out[8], multiplexer_7_out[7], multiplexer_7_out[6], multiplexer_7_out[5], multiplexer_7_out[4], multiplexer_7_out[3], multiplexer_7_out[2], multiplexer_7_out[1], multiplexer_7_out[0]);
  and and_1 (and_1_out, nor_1_out, Cmd[0]);
  and and_2 (jump, Cmd[15], or_1_out);
  assign and_3_out = multiplexer_6_out & multiplexer_9_out;  // AND_Gate and_3, 16 bits wide
  assign not_1_out = ~multiplexer_9_out;  // NOT_Gate not_1, 16 bits wide
  Multiplexer #(.select(2), .width(16), .enable("false")) multiplexer_2 (
    .in0(adder_1_out), .in1(adder_4_out), .in2(adder_3_out), .in3(adder_5_out), .out(multiplexer_2_out),
    .sel(Cmd[11:10]));
  and and_4 (and_4_out, multiplexer_7_out[15], Cmd[2]);
  or or_1 (or_1_out, and_1_out, and_4_out, and_5_out);
  Shifter #(.width(16), .shift("lr")) shifter_1 (.in(multiplexer_6_out), .\dist (4'b0001), .out(shifter_1_out));
  Multiplexer #(.select(2), .width(16), .enable("false")) multiplexer_3 (
    .in0(shifter_1_out), .in1(shifter_2_out), .in2(multiplier_1_out), .in3(divider_1_out),
    .out(multiplexer_3_out), .sel(Cmd[11:10]));
  assign or_2_out = multiplexer_6_out | multiplexer_9_out;  // OR_Gate or_2, 16 bits wide
  assign xor_1_out = multiplexer_6_out ^ multiplexer_9_out;  // XOR_Gate xor_1, 16 bits wide
  Multiplexer #(.select(2), .width(16), .enable("false")) multiplexer_4 (
    .in0(and_3_out), .in1(or_2_out), .in2(xor_1_out), .in3(not_2_out), .out(multiplexer_4_out),
    .sel(Cmd[11:10]));
  Adder #(.width(16)) adder_2 (.a(16'h1), .b(not_1_out), .out(adder_2_out));  // open: cin, cout
  nor nor_2 (nor_2_out, multiplexer_7_out[15], nor_1_out);
  and and_5 (and_5_out, Cmd[1], nor_2_out);
  Multiplexer #(.width(16), .enable("false")) multiplexer_5 (.in0(A), .in1(B), .out(multiplexer_5_out), .sel(Cmd[9]));
  Multiplexer #(.width(16), .enable("false")) multiplexer_6 (
    .in0(multiplexer_5_out), .in1({16{1'b0}}), .out(multiplexer_6_out), .sel(Cmd[8]));
  Shifter #(.width(16)) shifter_2 (.in(multiplexer_6_out), .\dist (4'b0001), .out(shifter_2_out));
  assign not_2_out = ~multiplexer_6_out;  // NOT_Gate not_2, 16 bits wide
  Adder #(.width(16)) adder_3 (.a(multiplexer_6_out), .b(16'h1), .out(adder_3_out));  // open: cin, cout
  Adder #(.width(16)) adder_4 (.a(multiplexer_6_out), .b(adder_2_out), .out(adder_4_out));  // open: cin, cout
  Multiplexer #(.select(2), .width(16), .enable("false")) multiplexer_7 (
    .in0(multiplexer_2_out), .in1(multiplexer_4_out), .in2(multiplexer_3_out), .in3(multiplexer_1_out),
    .out(multiplexer_7_out), .sel(Cmd[13:12]));
  Multiplexer #(.width(16), .enable("false")) multiplexer_8 (
    .in0({1'b0, Cmd[14:0]}), .in1(multiplexer_7_out), .out(\output ), .sel(Cmd[15]));
  Multiplier #(.width(16)) multiplier_1 (
    .a(multiplexer_6_out), .b(multiplexer_9_out), .out(multiplier_1_out));  // open: cin, cout
  Adder #(.width(16)) adder_5 (.a(multiplexer_6_out), .b({16{1'b1}}), .out(adder_5_out));  // open: cin, cout
  Divider #(.width(16)) divider_1 (
    .a(multiplexer_6_out), .b(multiplexer_9_out), .out(divider_1_out));  // open: upper, rem
  not not_3 (not_3_out, Cmd[15]);
  or or_3 (location[4], not_3_out, Cmd[7]);
  and and_6 (location[3], Cmd[6], Cmd[15]);
  Multiplexer #(.width(16), .enable("false")) multiplexer_9 (.in0(B), .in1(A), .out(multiplexer_9_out), .sel(Cmd[9]));
  and and_7 (location[1], Cmd[4], Cmd[15]);
  and and_8 (location[2], Cmd[5], Cmd[15]);
  and and_9 (location[0], Cmd[3], Cmd[15]);
endmodule
